// Logisim project TaskAnswers-Modificado.circ as structural Verilog
module BOARD_BIG_ASM (
  output out_1
);

  wire button_1_out, button_2_out, CLK, CLR, d_ff_1_q, not_1_out, Write, Write_ASCII;
  wire [6:0] ASCII;
  wire [7:0] counter_1_q;
  wire [23:0] Dir_INPUT, Dir_MEMORY;
  wire [31:0] INPUT, MEMORY_IN, MEMORY_OUT;

  Clock clock_1 (.out(CLK));
  D_Flip_Flop d_ff_1 (.clk(CLK), .D(1'b1), .Q(d_ff_1_q), .reset(button_1_out));  // open: Qn, preset, en
  Button button_1 (.out(button_1_out));
  Button button_2 (.out(button_2_out));
  D_Flip_Flop d_ff_2 (.clk(CLK), .D(d_ff_1_q), .Qn(CLR), .reset(button_1_out));  // open: Q, preset, en
  // Probe on INPUT
  // Probe on Dir_INPUT
  Task_81_Big_ASM task_81_big_asm_1 (
    .DATA_INPUT(INPUT), .MEMORY_IN(MEMORY_OUT), .start(button_2_out), .CLK(CLK), .CLR(CLR),
    .DIR_INPUT(Dir_INPUT), .MEMORY_OUT(MEMORY_IN), .DIR_MEMORY(Dir_MEMORY), .Write_OUTPUT(Write),
    .ASCII(ASCII), .Write_ASCII(Write_ASCII), .END(out_1));
  MEMORY memory_1 (.DIR(Dir_MEMORY), .DATA_IN(MEMORY_IN), .WRITE(Write), .CLK(CLK), .CLR(CLR), .DATA_OUT(MEMORY_OUT));
  INPUT input_1 (.DIR(Dir_INPUT), .CLK(CLK), .DATA_OUT(INPUT));
  Counter counter_1 (.load(1'b0), .count(not_1_out), .Q(counter_1_q), .clk(CLK), .clr(CLR));  // open: D, carry
  // Probe on counter_1_q
  not not_1 (not_1_out, out_1);
  TTY #(.rows(32), .cols(60)) tty_1 (.data(ASCII), .clk(CLK), .we(Write_ASCII), .clr(CLR));

  // Other names for the same wires on the sheet: END = out_1

  // Notes on the sheet:
  //   COUNTER
  //   BOARD
endmodule

module INPUT (
  input  [23:0] DIR,
  input  CLK,
  output [31:0] DATA_OUT
);

  RAM #(.addrWidth(24), .dataWidth(32)) ram_1 (.addr(DIR), .data(DATA_OUT), .clk(CLK), .ld(1'b1));  // open: sel, clr
endmodule

module MEMORY (
  input  [23:0] DIR,
  input  [31:0] DATA_IN,
  input  WRITE,
  input  CLK,
  input  CLR,
  output [31:0] DATA_OUT
);

  RAM #(.addrWidth(24), .dataWidth(32), .bus("separate")) ram_1 (
    .addr(DIR), .din(DATA_IN), .data(DATA_OUT), .str(WRITE), .clk(CLK), .clr(CLR));  // open: sel, ld
endmodule

module BIG_ASM (
  input  [31:0] DATA_INPUT,
  input  [31:0] MEMORY_IN,
  input  CLK,
  input  CLR,
  output [23:0] DIR_INPUT,
  output [31:0] MEMORY_OUT,
  output [23:0] DIR_MEMORY,
  output Write_OUTPUT,
  output [6:0] ASCII,
  output Write_ASCII,
  output END
);
endmodule

module PRINT_UDEC (
  input  [31:0] num,
  input  start,
  input  CLK,
  input  RST,
  output [6:0] ASCII,
  output Write_ASCII,
  output \end 
);

  wire _0_c, _0_n, demultiplexer_1_out0, demultiplexer_2_out0, demultiplexer_2_out1, demultiplexer_3_out0,
       demultiplexer_3_out1, IDLE_2_q, IDLE_3_q, IDLE_4_q, IDLE_q, Lc, Lc_0, Ln, Ln_0, or_1_out;
  wire [23:0] bit_extender_1_out;
  wire [31:0] c, c___1, c___1_t, divider_1_rem, memory_1_data_out, multiplexer_1_out, multiplexer_2_out,
       multiplexer_3_out, n, n___10, n___10___48;

  Multiplexer #(.width(32), .enable("false")) multiplexer_1 (
    .in0(num), .in1(n___10), .out(multiplexer_1_out), .sel(Lc_0));
  Divider #(.width(32)) divider_1 (.a(n), .b(32'ha), .out(n___10), .rem(divider_1_rem));  // open: upper
  Adder #(.width(32)) adder_1 (.a(divider_1_rem), .b(32'h30), .out(n___10___48));  // open: cin, cout
  or or_1 (or_1_out, demultiplexer_1_out0, \end );
  Register #(.width(32)) u_n (.D(multiplexer_1_out), .en(Ln), .Q(n), .clk(CLK), .clr(RST));
  D_Flip_Flop IDLE (.clk(CLK), .D(or_1_out), .Q(IDLE_q), .preset(RST));  // open: Qn, en, reset
  Demultiplexer #(.enable("false")) demultiplexer_1 (
    .out0(demultiplexer_1_out0), .out1(Ln_0), .in(IDLE_q), .sel(start));
  or or_2 (Write_ASCII, demultiplexer_3_out0, demultiplexer_2_out1);
  Multiplexer #(.width(32), .enable("false")) multiplexer_2 (
    .in0(c___1), .in1(c___1_t), .out(multiplexer_2_out), .sel(Write_ASCII));
  Adder #(.width(32)) adder_2 (.a(c), .b(32'h1), .out(c___1));  // open: cin, cout
  Subtractor #(.width(32)) subtractor_1 (.a(c), .b(32'h1), .out(c___1_t));  // open: bin, bout
  D_Flip_Flop IDLE_2 (.clk(CLK), .D(Ln_0), .Q(IDLE_2_q), .reset(RST));  // open: Qn, preset, en
  Register #(.width(32)) u_c (.D(multiplexer_2_out), .en(Lc), .Q(c), .clk(CLK), .clr(RST));
  or or_3 (Lc_0, IDLE_2_q, demultiplexer_3_out1);
  Multiplexer #(.width(32), .enable("false")) multiplexer_3 (
    .in0(c), .in1(c___1_t), .out(multiplexer_3_out), .sel(Write_ASCII));
  Comparator #(.width(32), .mode("unsigned")) comparator_1 (.a({32{1'b0}}), .b(n), .lt(_0_n));  // open: gt, eq
  Comparator #(.width(32), .mode("unsigned")) comparator_2 (.a({32{1'b0}}), .b(c), .lt(_0_c));  // open: gt, eq
  D_Flip_Flop IDLE_3 (.clk(CLK), .D(Write_ASCII), .Q(IDLE_3_q), .reset(RST));  // open: Qn, preset, en
  Demultiplexer #(.enable("false")) demultiplexer_2 (
    .out0(demultiplexer_2_out0), .out1(demultiplexer_2_out1), .in(IDLE_3_q), .sel(_0_c));
  Bit_Extender #(.in_width(32), .out_width(24)) bit_extender_1 (.in(multiplexer_3_out), .out(bit_extender_1_out));
  D_Flip_Flop IDLE_4 (.clk(CLK), .D(Lc_0), .Q(IDLE_4_q), .reset(RST));  // open: Qn, preset, en
  or or_4 (Lc, Lc_0, Write_ASCII);
  or or_5 (Ln, Ln_0, Lc_0);
  Demultiplexer #(.enable("false")) demultiplexer_3 (
    .out0(demultiplexer_3_out0), .out1(demultiplexer_3_out1), .in(IDLE_4_q), .sel(_0_n));
  D_Flip_Flop IDLE_5 (.clk(CLK), .D(demultiplexer_2_out0), .Q(\end ), .reset(RST));  // open: Qn, preset, en
  MEMORY memory_1 (
    .DIR(bit_extender_1_out), .DATA_IN(n___10___48), .WRITE(Lc_0), .CLK(CLK), .CLR(RST),
    .DATA_OUT(memory_1_data_out));
  Bit_Extender #(.in_width(32), .out_width(7)) bit_extender_2 (.in(memory_1_data_out), .out(ASCII));

  // Other names for the same wires on the sheet: Lc_1 = Write_ASCII; Sc = Write_ASCII; Ln_1 = Lc_0; Sn = Lc_0;
  //   Write = Lc_0
endmodule

module PRINT_DEC (
  input  [31:0] num,
  input  start,
  input  CLK,
  input  RST,
  output [6:0] ASCII,
  output Write_ASCII,
  output END
);

  wire demultiplexer_1_out0, demultiplexer_1_out1, demultiplexer_2_out0, demultiplexer_3_out0, end_t,
       IDLE_3_q, IDLE_q, or_1_out, or_2_out, or_3_out, S_ASCII, startUDEC, Write_ASCII_1;
  wire [6:0] ASCII_t;
  wire [31:0] multiplexer_1_out, negator_1_out;

  or or_1 (or_1_out, demultiplexer_1_out0, END);
  Negator #(.width(32)) negator_1 (.in(num), .out(negator_1_out));
  D_Flip_Flop IDLE (.clk(CLK), .D(or_1_out), .Q(IDLE_q), .preset(RST));  // open: Qn, en, reset
  Demultiplexer #(.enable("false")) demultiplexer_1 (
    .out0(demultiplexer_1_out0), .out1(demultiplexer_1_out1), .in(IDLE_q), .sel(start));
  Multiplexer #(.width(32), .enable("false")) multiplexer_1 (
    .in0(num), .in1(negator_1_out), .out(multiplexer_1_out), .sel(num[31]));
  Demultiplexer #(.enable("false")) demultiplexer_2 (
    .out0(demultiplexer_2_out0), .out1(S_ASCII), .in(demultiplexer_1_out1), .sel(num[31]));
  or or_2 (or_2_out, demultiplexer_2_out0, S_ASCII);
  D_Flip_Flop IDLE_2 (.clk(CLK), .D(or_2_out), .Q(startUDEC), .reset(RST));  // open: Qn, preset, en
  PRINT_UDEC print_udec_1 (
    .num(multiplexer_1_out), .start(startUDEC), .CLK(CLK), .RST(RST), .ASCII(ASCII_t),
    .Write_ASCII(Write_ASCII_1), .\end (end_t));
  D_Flip_Flop IDLE_3 (.clk(CLK), .D(or_3_out), .Q(IDLE_3_q), .reset(RST));  // open: Qn, preset, en
  or or_3 (or_3_out, startUDEC, demultiplexer_3_out0);
  Demultiplexer #(.enable("false")) demultiplexer_3 (
    .out0(demultiplexer_3_out0), .out1(END), .in(IDLE_3_q), .sel(end_t));
  Multiplexer #(.width(7), .enable("false")) multiplexer_2 (
    .in0(ASCII_t), .in1(7'b0101101), .out(ASCII), .sel(S_ASCII));
  or or_4 (Write_ASCII, S_ASCII, Write_ASCII_1);

  // Other names for the same wires on the sheet: sign = num[31]; Write_ASCII_0 = S_ASCII
endmodule

module TEST_PRINT (
  input  [31:0] in_1,
  output out_2
);

  wire button_1_out, button_2_out, CLK, CLR, d_ff_1_q, Write_ASCII;
  wire [6:0] ASCII;

  Button button_1 (.out(button_1_out));
  Clock clock_1 (.out(CLK));
  D_Flip_Flop d_ff_1 (.clk(CLK), .D(1'b1), .Q(d_ff_1_q), .reset(button_1_out));  // open: Qn, preset, en
  D_Flip_Flop d_ff_2 (.clk(CLK), .D(d_ff_1_q), .Qn(CLR), .reset(button_1_out));  // open: Q, preset, en
  Button button_2 (.out(button_2_out));
  PRINT_UDEC print_udec_1 ();  // open: num, start, CLK, RST, ASCII, Write_ASCII, end
  PRINT_DEC print_dec_1 (
    .num(in_1), .start(button_2_out), .CLK(CLK), .RST(CLR), .ASCII(ASCII), .Write_ASCII(Write_ASCII),
    .END(out_2));
  TTY #(.rows(32), .cols(60)) tty_1 (.data(ASCII), .clk(CLK), .we(Write_ASCII), .clr(CLR));
endmodule

module PRINT_MEMORY (
  input  [31:0] MEMORY_IN,
  input  start,
  input  CLK,
  input  RST,
  output [23:0] DIR_MEMORY,
  output End,
  output [6:0] ASCII,
  output Write_ASCII
);

  wire count___n, demultiplexer_1_out0, demultiplexer_2_out1, demultiplexer_3_out0, End_Print, IDLE_q, Lc,
       Ldir0, not_1_out, or_2_out, or_3_out, or_4_out, PRINT_q, Sc, Start_Print, W_ASCCI_0, W_ASCCI_1,
       WHILE_q;
  wire [6:0] ASCII_t;
  wire [23:0] Dir_1;
  wire [31:0] count, count_1, multiplexer_1_out, n;

  Register #(.width(32)) Rn (.D(MEMORY_IN), .en(Ldir0), .Q(n), .clk(CLK), .clr(RST));
  Comparator #(.width(32), .mode("unsigned")) comparator_1 (.a(count), .b(n), .lt(count___n));  // open: gt, eq
  D_Flip_Flop IDLE (.clk(CLK), .D(demultiplexer_1_out0), .Q(IDLE_q), .preset(RST));  // open: Qn, en, reset
  Demultiplexer #(.disabled(0), .enable("false")) demultiplexer_1 (
    .out0(demultiplexer_1_out0), .out1(Ldir0), .in(IDLE_q), .sel(start));
  or or_1 (Lc, Sc, Ldir0);
  Register #(.width(24)) RDir (.D(Dir_1), .en(or_2_out), .Q(DIR_MEMORY), .clk(CLK), .clr(RST));
  or or_2 (or_2_out, Lc, Ldir0);
  Adder #(.width(24)) adder_1 (.a(DIR_MEMORY), .b(24'h1), .out(Dir_1));  // open: cin, cout
  PRINT_DEC print_dec_1 (
    .num(MEMORY_IN), .start(Start_Print), .CLK(CLK), .RST(RST), .ASCII(ASCII_t), .Write_ASCII(W_ASCCI_0),
    .END(W_ASCCI_1));
  D_Flip_Flop WHILE (.clk(CLK), .D(Lc), .Q(WHILE_q), .reset(RST));  // open: Qn, preset, en
  not not_1 (not_1_out, count___n);
  Demultiplexer #(.disabled(0), .enable("false")) demultiplexer_2 (
    .out0(Start_Print), .out1(demultiplexer_2_out1), .in(WHILE_q), .sel(not_1_out));
  or or_3 (or_3_out, demultiplexer_2_out1, End);
  Multiplexer #(.width(32), .disabled(0), .enable("false")) multiplexer_1 (
    .in0({32{1'b0}}), .in1(count_1), .out(multiplexer_1_out), .sel(Sc));
  D_Flip_Flop PRINT_SPACE (.clk(CLK), .D(W_ASCCI_1), .Q(End_Print), .reset(RST));  // open: Qn, preset, en
  or or_4 (or_4_out, demultiplexer_3_out0, Start_Print);
  D_Flip_Flop u_END (.clk(CLK), .D(or_3_out), .Q(End), .reset(RST));  // open: Qn, preset, en
  Register #(.width(32)) Rcount (.D(multiplexer_1_out), .en(Lc), .Q(count), .clk(CLK), .clr(RST));
  Adder #(.width(32)) adder_2 (.a(count), .b(32'h1), .out(count_1));  // open: cin, cout
  Demultiplexer #(.disabled(0), .enable("false")) demultiplexer_3 (
    .out0(demultiplexer_3_out0), .out1(Sc), .in(PRINT_q), .sel(End_Print));
  D_Flip_Flop PRINT (.clk(CLK), .D(or_4_out), .Q(PRINT_q), .reset(RST));  // open: Qn, preset, en
  Multiplexer #(.width(7), .disabled(0), .enable("false")) multiplexer_2 (
    .in0(ASCII_t), .in1(7'b0100000), .out(ASCII), .sel(W_ASCCI_1));
  or or_5 (Write_ASCII, W_ASCCI_1, W_ASCCI_0);

  // Other names for the same wires on the sheet: Dir[23:0] = DIR_MEMORY; Ldir1 = Lc; Ln = Ldir0; MI[31:0] = MEMORY_IN;
  //   Reset = RST

  // Notes on the sheet:
  //   Input
  //   Data Path
  //   Control Unit
  //   Output
endmodule

module Task_20_Board (
  output out_1
);

  wire button_1_out, button_2_out, CLK, CLR, d_ff_1_q, not_1_out, Write, Write_ASCII;
  wire [6:0] ASCII;
  wire [7:0] counter_1_q;
  wire [23:0] Dir_INPUT, Dir_MEMORY;
  wire [31:0] INPUT, MEMORY_IN, MEMORY_OUT;

  Clock clock_1 (.out(CLK));
  D_Flip_Flop d_ff_1 (.clk(CLK), .D(1'b1), .Q(d_ff_1_q), .reset(button_1_out));  // open: Qn, preset, en
  Button button_1 (.out(button_1_out));
  Button button_2 (.out(button_2_out));
  D_Flip_Flop d_ff_2 (.clk(CLK), .D(d_ff_1_q), .Qn(CLR), .reset(button_1_out));  // open: Q, preset, en
  // Probe on INPUT
  // Probe on Dir_INPUT
  Task_20_Big_ASM task_20_big_asm_1 (
    .DATA_INPUT(INPUT), .MEMORY_IN(MEMORY_OUT), .CLK(CLK), .CLR(CLR), .DIR_INPUT(Dir_INPUT),
    .MEMORY_OUT(MEMORY_IN), .DIR_MEMORY(Dir_MEMORY), .Write_OUTPUT(Write), .ASCII(ASCII),
    .Write_ASCII(Write_ASCII), .END(out_1), .start(button_2_out));
  MEMORY memory_1 (.DIR(Dir_MEMORY), .DATA_IN(MEMORY_IN), .WRITE(Write), .CLK(CLK), .CLR(CLR), .DATA_OUT(MEMORY_OUT));
  INPUT input_1 (.DIR(Dir_INPUT), .CLK(CLK), .DATA_OUT(INPUT));
  Counter counter_1 (.load(1'b0), .count(not_1_out), .Q(counter_1_q), .clk(CLK), .clr(CLR));  // open: D, carry
  // Probe on counter_1_q
  not not_1 (not_1_out, out_1);
  TTY #(.rows(32), .cols(60)) tty_1 (.data(ASCII), .clk(CLK), .we(Write_ASCII), .clr(CLR));

  // Other names for the same wires on the sheet: END = out_1

  // Notes on the sheet:
  //   COUNTER
  //   BOARD
endmodule

module Task_20_Big_ASM (
  input  [31:0] DATA_INPUT,
  input  [31:0] MEMORY_IN,
  input  start,
  input  CLK,
  input  CLR,
  output [23:0] DIR_INPUT,
  output [31:0] MEMORY_OUT,
  output [23:0] DIR_MEMORY,
  output Write_OUTPUT,
  output [6:0] ASCII,
  output Write_ASCII,
  output END
);

  wire count____b, count___a, count__a, End_Print, La, Lb, Lc, Ld, Ll, Lm, Ln, max__L, Sc, StartPrint;
  wire [31:0] Max;

  Task_20_Data_Path task_20_data_path_1 (
    .Value(DATA_INPUT), .La(La), .Lb(Lb), .Ln(Ln), .Ll(Ll), .Lcount(Lc), .Scount(Sc), .Lmax(Lm), .Ldir(Ld),
    .CLK(CLK), .Reset(CLR), .Dir_1(DIR_INPUT), .Max(Max), .out_14(count____b), .out_15(count___a),
    .out_16(count__a), .out_17(max__L));
  PRINT_DEC print_dec_1 (
    .num(Max), .start(StartPrint), .CLK(CLK), .RST(CLR), .ASCII(ASCII), .Write_ASCII(Write_ASCII),
    .END(End_Print));
  Task_20_Control_Unit task_20_control_unit_1 (
    .start(start), .CLK(CLK), .Reset(CLR), .count____b(count____b), .count___a(count___a),
    .count__a(count__a), .max__L(max__L), .La(La), .Lb(Lb), .Ln(Ln), .Ll(Ll), .Lcount(Lc), .Scount(Sc),
    .Lmax(Lm), .Start_Print(StartPrint), .Ldir(Ld), .END(END), .End_Print(End_Print));

  // Other names for the same wires on the sheet: DI[31:0] = DATA_INPUT; Dir_1[23:0] = DIR_INPUT; MI[31:0] = MEMORY_IN;
  //   W_ASCCI = Write_ASCII

  // Notes on the sheet:
  //   Input
  //   ASM
  //   Output
endmodule

module Task_20_Data_Path (
  input  [31:0] Value,
  input  La,
  input  Lb,
  input  Ln,
  input  Ll,
  input  Lcount,
  input  Scount,
  input  Lmax,
  input  Ldir,
  input  CLK,
  input  Reset,
  output [23:0] Dir_1,
  output [31:0] Max,
  output out_14,
  output out_15,
  output out_16,
  output out_17
);

  wire comparator_3_eq, comparator_3_lt;
  wire [23:0] Dir_1_t;
  wire [31:0] a, b, count, count_1, L, multiplexer_1_out, n;

  Register #(.width(32)) Ra (.D(Value), .en(La), .Q(a), .clk(CLK), .clr(Reset));
  Multiplexer #(.width(32), .disabled(0), .enable("false")) multiplexer_1 (
    .in0({32{1'b0}}), .in1(count_1), .out(multiplexer_1_out), .sel(Scount));
  Adder #(.width(32)) adder_1 (.a(count), .b(32'h1), .out(count_1));  // open: cin, cout
  Register #(.width(32)) Rcount (.D(multiplexer_1_out), .en(Lcount), .Q(count), .clk(CLK), .clr(Reset));
  Register #(.width(32)) Rb (.D(Value), .en(Lb), .Q(b), .clk(CLK), .clr(Reset));
  Comparator #(.width(32), .mode("unsigned")) comparator_1 (.a(count), .b(a), .gt(out_16));  // open: eq, lt
  Comparator #(.width(32), .mode("unsigned")) comparator_2 (.a(Max), .b(Value), .lt(out_17));  // open: gt, eq
  Register #(.width(32)) Rmax (.D(Value), .en(Lmax), .Q(Max), .clk(CLK), .clr(Reset));
  Register #(.width(32)) Rn (.D(Value), .en(Ln), .Q(n), .clk(CLK), .clr(Reset));
  Comparator #(.width(32), .mode("unsigned")) comparator_3 (
    .a(count), .b(b), .eq(comparator_3_eq), .lt(comparator_3_lt));  // open: gt
  Comparator #(.width(32), .mode("unsigned")) comparator_4 (.a(count), .b(a), .eq(out_15));  // open: gt, lt
  or or_1 (out_14, comparator_3_eq, comparator_3_lt);
  Register #(.width(24)) RDir (.D(Dir_1_t), .en(Ldir), .Q(Dir_1), .clk(CLK), .clr(Reset));
  Adder #(.width(24)) adder_2 (.a(Dir_1), .b(24'h1), .out(Dir_1_t));  // open: cin, cout
  Register #(.width(32)) RL (.D(Value), .en(Ll), .Q(L), .clk(CLK), .clr(Reset));

  // Other names for the same wires on the sheet: count____b = out_14; count___a = out_15; count__a = out_16;
  //   Dir[23:0] = Dir_1; Lc = Lcount; max__L = out_17; Sc = Scount

  // Notes on the sheet:
  //   Input
  //   Registers
  //   Flags
  //   Output
endmodule

module Task_20_Control_Unit (
  input  start,
  input  CLK,
  input  Reset,
  input  End_Print,
  input  count____b,
  input  count___a,
  input  count__a,
  input  max__L,
  output La,
  output Lb,
  output Lmax,
  output Ln,
  output Ll,
  output Lcount,
  output Scount,
  output Ldir,
  output Start_Print,
  output END
);

  wire demultiplexer_1_out0, demultiplexer_3_out0, demultiplexer_4_out0, demultiplexer_5_out0,
       demultiplexer_5_out1, demultiplexer_6_out0, demultiplexer_6_out1, IDLE_q, Lm0, Lm1, or_5_out,
       or_6_out, or_7_out, PRINT_q, WAIT_3_q, WHILE_q;

  D_Flip_Flop IDLE (.clk(CLK), .D(demultiplexer_1_out0), .Q(IDLE_q), .preset(Reset));  // open: Qn, en, reset
  Demultiplexer #(.disabled(0), .enable("false")) demultiplexer_1 (
    .out0(demultiplexer_1_out0), .out1(La), .in(IDLE_q), .sel(start));
  D_Flip_Flop WAIT (.clk(CLK), .D(La), .Q(Lb), .reset(Reset));  // open: Qn, preset, en
  D_Flip_Flop WAIT_2 (.clk(CLK), .D(Lb), .Q(Ln), .reset(Reset));  // open: Qn, preset, en
  D_Flip_Flop WAIT_3 (.clk(CLK), .D(Ln), .Q(WAIT_3_q), .reset(Reset));  // open: Qn, preset, en
  or or_1 (Lmax, Lm0, Lm1);
  or or_2 (Ldir, La, Lb, Ln, Scount);
  or or_3 (Scount, Lm1, demultiplexer_3_out0, demultiplexer_5_out0);
  or or_4 (Lcount, WAIT_3_q, Scount);
  Demultiplexer #(.disabled(0), .enable("false")) demultiplexer_2 (
    .out0(Start_Print), .out1(Ll), .in(WHILE_q), .sel(count____b));
  D_Flip_Flop WHILE (.clk(CLK), .D(Lcount), .Q(WHILE_q), .reset(Reset));  // open: Qn, preset, en
  Demultiplexer #(.disabled(0), .enable("false")) demultiplexer_3 (
    .out0(demultiplexer_3_out0), .out1(Lm1), .in(demultiplexer_5_out1), .sel(max__L));
  Demultiplexer #(.disabled(0), .enable("false")) demultiplexer_4 (
    .out0(demultiplexer_4_out0), .out1(Lm0), .in(Ll), .sel(count___a));
  or or_5 (or_5_out, demultiplexer_4_out0, Lm0);
  Demultiplexer #(.disabled(0), .enable("false")) demultiplexer_5 (
    .out0(demultiplexer_5_out0), .out1(demultiplexer_5_out1), .in(or_5_out), .sel(count__a));
  or or_6 (or_6_out, demultiplexer_6_out0, Start_Print);
  D_Flip_Flop PRINT (.clk(CLK), .D(or_6_out), .Q(PRINT_q), .reset(Reset));  // open: Qn, preset, en
  Demultiplexer #(.disabled(0), .enable("false")) demultiplexer_6 (
    .out0(demultiplexer_6_out0), .out1(demultiplexer_6_out1), .in(PRINT_q), .sel(End_Print));
  or or_7 (or_7_out, demultiplexer_6_out1, END);
  D_Flip_Flop u_END (.clk(CLK), .D(or_7_out), .Q(END), .reset(Reset));  // open: Qn, preset, en

  // Other names for the same wires on the sheet: Lc = Lcount; Ldir0 = La; Ldir1 = Lb; Ldir2 = Ln; Ldir3 = Scount;
  //   Sc = Scount

  // Notes on the sheet:
  //   Output
  //   Input
endmodule

module Task_45_Board (
  output out_1
);

  wire button_1_out, button_2_out, CLK, CLR, d_ff_1_q, not_1_out, Write, Write_ASCII;
  wire [6:0] ASCII;
  wire [7:0] counter_1_q;
  wire [23:0] Dir_INPUT, Dir_MEMORY;
  wire [31:0] INPUT, MEMORY_IN, MEMORY_OUT;

  Clock clock_1 (.out(CLK));
  D_Flip_Flop d_ff_1 (.clk(CLK), .D(1'b1), .Q(d_ff_1_q), .reset(button_1_out));  // open: Qn, preset, en
  Button button_1 (.out(button_1_out));
  Button button_2 (.out(button_2_out));
  D_Flip_Flop d_ff_2 (.clk(CLK), .D(d_ff_1_q), .Qn(CLR), .reset(button_1_out));  // open: Q, preset, en
  // Probe on INPUT
  // Probe on Dir_INPUT
  Task_45_Big_ASM task_45_big_asm_1 (
    .DATA_INPUT(INPUT), .MEMORY_IN(MEMORY_OUT), .CLK(CLK), .CLR(CLR), .DIR_INPUT(Dir_INPUT),
    .MEMORY_OUT(MEMORY_IN), .DIR_MEMORY(Dir_MEMORY), .Write_OUTPUT(Write), .ASCII(ASCII),
    .Write_ASCII(Write_ASCII), .END(out_1), .start(button_2_out));
  MEMORY memory_1 (.DIR(Dir_MEMORY), .DATA_IN(MEMORY_IN), .WRITE(Write), .CLK(CLK), .CLR(CLR), .DATA_OUT(MEMORY_OUT));
  INPUT input_1 (.DIR(Dir_INPUT), .CLK(CLK), .DATA_OUT(INPUT));
  // Probe on counter_1_q
  Counter counter_1 (.load(1'b0), .count(not_1_out), .Q(counter_1_q), .clk(CLK), .clr(CLR));  // open: D, carry
  not not_1 (not_1_out, out_1);
  TTY #(.rows(32), .cols(60)) tty_1 (.data(ASCII), .clk(CLK), .we(Write_ASCII), .clr(CLR));

  // Other names for the same wires on the sheet: END = out_1

  // Notes on the sheet:
  //   COUNTER
  //   BOARD
endmodule

module Task_45_Big_ASM (
  input  [31:0] DATA_INPUT,
  input  [31:0] MEMORY_IN,
  input  start,
  input  CLK,
  input  CLR,
  output [23:0] DIR_INPUT,
  output [31:0] MEMORY_OUT,
  output [23:0] DIR_MEMORY,
  output Write_OUTPUT,
  output [6:0] ASCII,
  output Write_ASCII,
  output END
);

  wire count__n, End_Print, Lc, Ldir, Ll, Ln, Lsum, Lx, Sc, StartPrint, Value___x;
  wire [31:0] sum;

  Task_45_Data_Path task_45_data_path_1 (
    .Value(DATA_INPUT), .Lx(Lx), .Ln(Ln), .Ll(Ll), .Lcount(Lc), .Lsum(Lsum), .Ldir(Ldir), .CLK(CLK),
    .Reset(CLR), .Dir_1(DIR_INPUT), .Sum(sum), .out_13(count__n), .out_14(Value___x), .Scount(Sc));
  PRINT_DEC print_dec_1 (
    .num(sum), .start(StartPrint), .CLK(CLK), .RST(CLR), .ASCII(ASCII), .Write_ASCII(Write_ASCII),
    .END(End_Print));
  Task_45_Control_Unit task_45_control_unit_1 (
    .start(start), .CLK(CLK), .Reset(CLR), .End_Print(End_Print), .count__0(count__n), .Value___x(Value___x),
    .Lx(Lx), .Ln(Ln), .Ll(Ll), .Lc(Lc), .Ldir(Ldir), .Lsum(Lsum), .End(END), .Start_Print(StartPrint), .Sc(Sc));

  // Other names for the same wires on the sheet: DI[31:0] = DATA_INPUT; Dir_1[23:0] = DIR_INPUT; MI[31:0] = MEMORY_IN;
  //   W_ASCCI = Write_ASCII

  // Notes on the sheet:
  //   Input
  //   ASM
  //   Output
endmodule

module Task_45_Data_Path (
  input  [31:0] Value,
  input  Lx,
  input  Ln,
  input  Ll,
  input  Scount,
  input  Lcount,
  input  Lsum,
  input  Ldir,
  input  CLK,
  input  Reset,
  output [23:0] Dir_1,
  output [31:0] Sum,
  output out_13,
  output out_14
);

  wire comparator_1_gt;
  wire [23:0] Dir_1_t;
  wire [31:0] count, count_1, L, multiplexer_1_out, n, n_1, Nsum, x;

  Multiplexer #(.width(32), .disabled(0), .enable("false")) multiplexer_1 (
    .in0(n_1), .in1(count_1), .out(multiplexer_1_out), .sel(Scount));
  Register #(.width(32)) Rx (.D(Value), .en(Lx), .Q(x), .clk(CLK), .clr(Reset));
  Register #(.width(32)) Rcount (.D(multiplexer_1_out), .en(Lcount), .Q(count), .clk(CLK), .clr(Reset));
  Subtractor #(.width(32)) subtractor_1 (.a(count), .b(32'h1), .out(count_1));  // open: bin, bout
  Subtractor #(.width(32)) subtractor_2 (.a(n), .b(32'h1), .out(n_1));  // open: bin, bout
  Comparator #(.width(32)) comparator_1 (.a(count), .b({32{1'b1}}), .gt(comparator_1_gt));  // open: eq, lt
  buf or_1 (out_13, comparator_1_gt);  // OR_Gate
  Register #(.width(32)) Rn (.D(Value), .en(Ln), .Q(n), .clk(CLK), .clr(Reset));
  Register #(.width(32)) Rsum (.D(Nsum), .en(Lsum), .Q(Sum), .clk(CLK), .clr(Reset));
  Adder #(.width(32)) adder_1 (.a(Sum), .b(Value), .out(Nsum));  // open: cin, cout
  Register #(.width(32)) RL (.D(Value), .en(Ll), .Q(L), .clk(CLK), .clr(Reset));
  Comparator #(.width(32), .mode("unsigned")) comparator_2 (.a(Value), .b(x), .gt(out_14));  // open: eq, lt
  Adder #(.width(24)) adder_2 (.a(Dir_1), .b(24'h1), .out(Dir_1_t));  // open: cin, cout
  Register #(.width(24)) RDir (.D(Dir_1_t), .en(Ldir), .Q(Dir_1), .clk(CLK), .clr(Reset));

  // Other names for the same wires on the sheet: count__0 = out_13; Dir[23:0] = Dir_1; Lc = Lcount; Sc = Scount;
  //   Value___x = out_14

  // Notes on the sheet:
  //   Input
  //   Registers
  //   Flags
  //   Output
endmodule

module Task_45_Control_Unit (
  input  start,
  input  CLK,
  input  Reset,
  input  End_Print,
  input  count__0,
  input  Value___x,
  output Lx,
  output Sc,
  output Ln,
  output Lc,
  output Ldir,
  output Ll,
  output Lsum,
  output Start_Print,
  output End
);

  wire demultiplexer_1_out0, demultiplexer_2_out0, demultiplexer_3_out0, demultiplexer_4_out0,
       demultiplexer_4_out1, IDLE_q, or_5_out, PRINT_q, WAIT_2_q, WHILE_q;

  Demultiplexer #(.disabled(0), .enable("false")) demultiplexer_1 (
    .out0(demultiplexer_1_out0), .out1(Lx), .in(IDLE_q), .sel(start));
  D_Flip_Flop IDLE (.clk(CLK), .D(demultiplexer_1_out0), .Q(IDLE_q), .preset(Reset));  // open: Qn, en, reset
  D_Flip_Flop WAIT (.clk(CLK), .D(Lx), .Q(Ln), .reset(Reset));  // open: Qn, preset, en
  D_Flip_Flop WAIT_2 (.clk(CLK), .D(Ln), .Q(WAIT_2_q), .reset(Reset));  // open: Qn, preset, en
  or or_1 (Sc, Lsum, demultiplexer_3_out0);
  or or_2 (Ldir, Lx, Ln, Sc);
  or or_3 (Lc, WAIT_2_q, Sc);
  D_Flip_Flop WHILE (.clk(CLK), .D(Lc), .Q(WHILE_q), .reset(Reset));  // open: Qn, preset, en
  Demultiplexer #(.disabled(0), .enable("false")) demultiplexer_2 (
    .out0(demultiplexer_2_out0), .out1(Ll), .in(WHILE_q), .sel(count__0));
  Demultiplexer #(.disabled(0), .enable("false")) demultiplexer_3 (
    .out0(demultiplexer_3_out0), .out1(Lsum), .in(Ll), .sel(Value___x));
  or or_4 (Start_Print, demultiplexer_4_out0, demultiplexer_2_out0);
  D_Flip_Flop PRINT (.clk(CLK), .D(Start_Print), .Q(PRINT_q), .reset(Reset));  // open: Qn, preset, en
  Demultiplexer #(.disabled(0), .enable("false")) demultiplexer_4 (
    .out0(demultiplexer_4_out0), .out1(demultiplexer_4_out1), .in(PRINT_q), .sel(End_Print));
  or or_5 (or_5_out, demultiplexer_4_out1, End);
  D_Flip_Flop u_END (.clk(CLK), .D(or_5_out), .Q(End), .reset(Reset));  // open: Qn, preset, en

  // Other names for the same wires on the sheet: Ldir0 = Lx; Ldir1 = Ln; Ldir3 = Sc

  // Notes on the sheet:
  //   Output
  //   Input
endmodule

module Task_81_Board (
  output out_1
);

  wire button_1_out, button_2_out, CLK, CLR, d_ff_1_q, not_1_out, Write, Write_ASCII;
  wire [6:0] ASCII;
  wire [7:0] counter_1_q;
  wire [23:0] Dir_INPUT, Dir_MEMORY;
  wire [31:0] INPUT, MEMORY_IN, MEMORY_OUT;

  Clock clock_1 (.out(CLK));
  D_Flip_Flop d_ff_1 (.clk(CLK), .D(1'b1), .Q(d_ff_1_q), .reset(button_1_out));  // open: Qn, preset, en
  Button button_1 (.out(button_1_out));
  Button button_2 (.out(button_2_out));
  D_Flip_Flop d_ff_2 (.clk(CLK), .D(d_ff_1_q), .Qn(CLR), .reset(button_1_out));  // open: Q, preset, en
  // Probe on INPUT
  // Probe on Dir_INPUT
  Task_81_Big_ASM task_81_big_asm_1 (
    .DATA_INPUT(INPUT), .MEMORY_IN(MEMORY_OUT), .start(button_2_out), .CLK(CLK), .CLR(CLR),
    .DIR_INPUT(Dir_INPUT), .MEMORY_OUT(MEMORY_IN), .DIR_MEMORY(Dir_MEMORY), .Write_OUTPUT(Write),
    .ASCII(ASCII), .Write_ASCII(Write_ASCII), .END(out_1));
  MEMORY memory_1 (.DIR(Dir_MEMORY), .DATA_IN(MEMORY_IN), .WRITE(Write), .CLK(CLK), .CLR(CLR), .DATA_OUT(MEMORY_OUT));
  INPUT input_1 (.DIR(Dir_INPUT), .CLK(CLK), .DATA_OUT(INPUT));
  Counter counter_1 (.load(1'b0), .count(not_1_out), .Q(counter_1_q), .clk(CLK), .clr(CLR));  // open: D, carry
  // Probe on counter_1_q
  not not_1 (not_1_out, out_1);
  TTY #(.rows(32), .cols(60)) tty_1 (.data(ASCII), .clk(CLK), .we(Write_ASCII), .clr(CLR));

  // Other names for the same wires on the sheet: END = out_1

  // Notes on the sheet:
  //   COUNTER
  //   BOARD
endmodule

module Task_81_Big_ASM (
  input  [31:0] DATA_INPUT,
  input  [31:0] MEMORY_IN,
  input  start,
  input  CLK,
  input  CLR,
  output [23:0] DIR_INPUT,
  output [31:0] MEMORY_OUT,
  output [23:0] DIR_MEMORY,
  output Write_OUTPUT,
  output [6:0] ASCII,
  output Write_ASCII,
  output END
);

  wire count__n, End_Print, Lc, Ldir, Ll, Lmax, Ln, max__L, PrintMemory, Sc, StartPrint;
  wire [23:0] Mer, MerP;

  Task_81_Data_Path task_81_data_path_1 (
    .Value(DATA_INPUT), .Ln(Ln), .Ll(Ll), .Lcount(Lc), .Scount(Sc), .Lmax(Lmax), .Ldir(Ldir), .CLK(CLK),
    .Reset(CLR), .Dir_1(DIR_INPUT), .Max(MEMORY_OUT), .count___n(count__n), .max__L(max__L));
  Subtractor #(.width(24)) subtractor_1 (.a(DIR_INPUT), .b(24'h1), .out(Mer));  // open: bin, bout
  PRINT_MEMORY print_memory_1 (
    .MEMORY_IN(MEMORY_IN), .start(StartPrint), .CLK(CLK), .RST(CLR), .DIR_MEMORY(MerP), .End(End_Print),
    .ASCII(ASCII), .Write_ASCII(Write_ASCII));
  D_Flip_Flop d_ff_1 (.clk(CLK), .Q(PrintMemory), .preset(StartPrint), .reset(CLR));  // open: D, Qn, en
  Task_81_Control_Unit task_81_control_unit_1 (
    .start(start), .CLK(CLK), .Reset(CLR), .End_Print(End_Print), .count__n(count__n), .max__L(max__L),
    .Ln(Ln), .Sc(Sc), .Ldir(Ldir), .Ll(Ll), .Lc(Lc), .Start_Print(StartPrint), .End(END), .Lmax(Lmax));
  Multiplexer #(.width(24), .disabled(0), .enable("false")) multiplexer_1 (
    .in0(Mer), .in1(MerP), .out(DIR_MEMORY), .sel(PrintMemory));
  not not_1 (Write_OUTPUT, PrintMemory);

  // Other names for the same wires on the sheet: DI[31:0] = DATA_INPUT; Dir_1[23:0] = DIR_INPUT;
  //   max[31:0] = MEMORY_OUT; MI[31:0] = MEMORY_IN; W_ASCCI = Write_ASCII

  // Notes on the sheet:
  //   Input
  //   ASM
  //   Output
endmodule

module Task_81_Data_Path (
  input  [31:0] Value,
  input  Ln,
  input  Ll,
  input  Lcount,
  input  Scount,
  input  Lmax,
  input  Ldir,
  input  CLK,
  input  Reset,
  output [23:0] Dir_1,
  output [31:0] Max,
  output count___n,
  output max__L
);

  wire [23:0] Dir_1_t;
  wire [31:0] count, count_1, L, multiplexer_1_out, n;

  Register #(.width(32)) Rn (.D(Value), .en(Ln), .Q(n), .clk(CLK), .clr(Reset));
  Multiplexer #(.width(32), .disabled(0), .enable("false")) multiplexer_1 (
    .in0({32{1'b0}}), .in1(count_1), .out(multiplexer_1_out), .sel(Scount));
  Comparator #(.width(32), .mode("unsigned")) comparator_1 (.a(count), .b(n), .lt(count___n));  // open: gt, eq
  Register #(.width(32)) Rcount (.D(multiplexer_1_out), .en(Lcount), .Q(count), .clk(CLK), .clr(Reset));
  Adder #(.width(32)) adder_1 (.a(count), .b(32'h1), .out(count_1));  // open: cin, cout
  Register #(.width(32)) RL (.D(Value), .en(Ll), .Q(L), .clk(CLK), .clr(Reset));
  Register #(.width(24)) RDir (.D(Dir_1_t), .en(Ldir), .Q(Dir_1), .clk(CLK), .clr(Reset));
  Adder #(.width(24)) adder_2 (.a(Dir_1), .b(24'h1), .out(Dir_1_t));  // open: cin, cout
  Comparator #(.width(32), .mode("unsigned")) comparator_2 (.a(Max), .b(Value), .lt(max__L));  // open: gt, eq
  Register #(.width(32)) Rmax (.D(Value), .en(Lmax), .Q(Max), .clk(CLK), .clr(Reset));

  // Other names for the same wires on the sheet: Dir[23:0] = Dir_1; Lc = Lcount; Sc = Scount

  // Notes on the sheet:
  //   Input
  //   Registers
  //   Flags
  //   Output
endmodule

module Task_81_Control_Unit (
  input  start,
  input  CLK,
  input  Reset,
  input  End_Print,
  input  count__n,
  input  max__L,
  output Ln,
  output Sc,
  output Ldir,
  output Ll,
  output Lc,
  output Start_Print,
  output End,
  output Lmax
);

  wire demultiplexer_1_out0, demultiplexer_2_out1, demultiplexer_3_out0, demultiplexer_4_out0,
       demultiplexer_4_out1, IDLE_q, Lmax2, or_5_out, or_6_out, PRINT_q, WHILE_q;

  Demultiplexer #(.disabled(0), .enable("false")) demultiplexer_1 (
    .out0(demultiplexer_1_out0), .out1(Ln), .in(IDLE_q), .sel(start));
  D_Flip_Flop IDLE (.clk(CLK), .D(demultiplexer_1_out0), .Q(IDLE_q), .preset(Reset));  // open: Qn, en, reset
  D_Flip_Flop WAIT (.clk(CLK), .D(Ln), .Q(Ll), .reset(Reset));  // open: Qn, preset, en
  or or_1 (Sc, Lmax2, demultiplexer_3_out0);
  or or_2 (Lc, Ll, Sc);
  or or_3 (Ldir, Ln, Lc);
  or or_4 (Lmax, Ln, Ll, Lmax2);
  Demultiplexer #(.disabled(0), .enable("false")) demultiplexer_2 (
    .out0(Start_Print), .out1(demultiplexer_2_out1), .in(WHILE_q), .sel(count__n));
  D_Flip_Flop WHILE (.clk(CLK), .D(Lc), .Q(WHILE_q), .reset(Reset));  // open: Qn, preset, en
  Demultiplexer #(.disabled(0), .enable("false")) demultiplexer_3 (
    .out0(demultiplexer_3_out0), .out1(Lmax2), .in(demultiplexer_2_out1), .sel(max__L));
  or or_5 (or_5_out, demultiplexer_4_out0, Start_Print);
  D_Flip_Flop PRINT (.clk(CLK), .D(or_5_out), .Q(PRINT_q), .reset(Reset));  // open: Qn, preset, en
  Demultiplexer #(.disabled(0), .enable("false")) demultiplexer_4 (
    .out0(demultiplexer_4_out0), .out1(demultiplexer_4_out1), .in(PRINT_q), .sel(End_Print));
  or or_6 (or_6_out, demultiplexer_4_out1, End);
  D_Flip_Flop u_END (.clk(CLK), .D(or_6_out), .Q(End), .reset(Reset));  // open: Qn, preset, en

  // Other names for the same wires on the sheet: Ldir1 = Lc; Ldir0 = Ln; Lmax0 = Ln; Lmax1 = Ll

  // Notes on the sheet:
  //   Output
  //   Input
endmodule

module Task_66_Board (
  output out_1
);

  wire button_1_out, button_2_out, CLK, CLR, d_ff_1_q, not_1_out, Write, Write_ASCII;
  wire [6:0] ASCII;
  wire [7:0] counter_1_q;
  wire [23:0] Dir_INPUT, Dir_MEMORY;
  wire [31:0] INPUT, MEMORY_IN, MEMORY_OUT;

  Clock clock_1 (.out(CLK));
  D_Flip_Flop d_ff_1 (.clk(CLK), .D(1'b1), .Q(d_ff_1_q), .reset(button_1_out));  // open: Qn, preset, en
  Button button_1 (.out(button_1_out));
  Button button_2 (.out(button_2_out));
  D_Flip_Flop d_ff_2 (.clk(CLK), .D(d_ff_1_q), .Qn(CLR), .reset(button_1_out));  // open: Q, preset, en
  // Probe on INPUT
  // Probe on Dir_INPUT
  Task_66_Big_ASM task_66_big_asm_1 (
    .DATA_INPUT(INPUT), .MEMORY_IN(MEMORY_OUT), .start(button_2_out), .CLK(CLK), .CLR(CLR),
    .DIR_INPUT(Dir_INPUT), .MEMORY_OUT(MEMORY_IN), .DIR_MEMORY(Dir_MEMORY), .Write_OUTPUT(Write),
    .ASCII(ASCII), .Write_ASCII(Write_ASCII), .END(out_1));
  MEMORY memory_1 (.DIR(Dir_MEMORY), .DATA_IN(MEMORY_IN), .WRITE(Write), .CLK(CLK), .CLR(CLR), .DATA_OUT(MEMORY_OUT));
  INPUT input_1 (.DIR(Dir_INPUT), .CLK(CLK), .DATA_OUT(INPUT));
  // Probe on counter_1_q
  Counter counter_1 (.load(1'b0), .count(not_1_out), .Q(counter_1_q), .clk(CLK), .clr(CLR));  // open: D, carry
  not not_1 (not_1_out, out_1);
  TTY #(.rows(32), .cols(60)) tty_1 (.data(ASCII), .clk(CLK), .we(Write_ASCII), .clr(CLR));

  // Other names for the same wires on the sheet: END = out_1

  // Notes on the sheet:
  //   COUNTER
  //   BOARD
endmodule

module Task_66_Big_ASM (
  input  [31:0] DATA_INPUT,
  input  [31:0] MEMORY_IN,
  input  start,
  input  CLK,
  input  CLR,
  output [23:0] DIR_INPUT,
  output [31:0] MEMORY_OUT,
  output [23:0] DIR_MEMORY,
  output Write_OUTPUT,
  output [6:0] ASCII,
  output Write_ASCII,
  output END
);

  wire count1_n1, count2_n2, count___n1_n2, e1_e2, End_Print, Lc, Lc1, Lc2, Ldi2, Ldir, Ldir1, Le1, Le2, Ln,
       Ln1, Ln2, PrintMemory, Sc, Sc1, Sc2, Sdir2, StartPrint;
  wire [23:0] MemoDIr, MerP;

  Task_66_Data_Path task_66_data_path_1 (
    .Value(DATA_INPUT), .Lcount(Lc), .Scount(Sc), .Ldir(Ldir), .Ln(Ln), .Le1(Le1), .Le2(Le2), .Ln1(Ln1),
    .Ln2(Ln2), .Lcount1(Lc1), .Lcount2(Lc2), .Scount1(Sc1), .Scount2(Sc2), .Ldir1(Ldir1), .Ldir2(Ldi2),
    .Sdir2(Sdir2), .CLK(CLK), .Reset(CLR), .Dir_1(MemoDIr), .Dir1o2(DIR_INPUT), .E1o2(MEMORY_OUT),
    .e1_e2(e1_e2), .count1_n1(count1_n1), .count2_n2(count2_n2), .count___n1_n2(count___n1_n2));
  PRINT_MEMORY print_memory_1 (
    .MEMORY_IN(MEMORY_IN), .start(StartPrint), .CLK(CLK), .RST(CLR), .DIR_MEMORY(MerP), .End(End_Print),
    .ASCII(ASCII), .Write_ASCII(Write_ASCII));
  D_Flip_Flop d_ff_1 (.clk(CLK), .Q(PrintMemory), .preset(StartPrint), .reset(CLR));  // open: D, Qn, en
  Task_66_Control_Unit task_66_control_unit_1 (
    .start(start), .CLK(CLK), .Reset(CLR), .End_Print(End_Print), .e1_e2(e1_e2), .count1_n1(count1_n1),
    .count2_n2(count2_n2), .count___n1_n2(count___n1_n2), .out_9(Le1), .out_10(Ln1), .out_11(Lc1),
    .out_12(Sc1), .out_13(Ldir1), .out_14(Le2), .out_15(Ln2), .out_16(Lc2), .out_17(Sc2), .out_18(Ldi2),
    .out_19(Sdir2), .out_20(Ln), .out_21(Sc), .out_22(Lc), .out_23(Ldir), .Start_Print(StartPrint), .End(END));
  Multiplexer #(.width(24), .disabled(0), .enable("false")) multiplexer_1 (
    .in0(MemoDIr), .in1(MerP), .out(DIR_MEMORY), .sel(PrintMemory));
  not not_1 (Write_OUTPUT, PrintMemory);

  // Other names for the same wires on the sheet: DI[31:0] = DATA_INPUT; Dir1o2[23:0] = DIR_INPUT;
  //   MI[31:0] = MEMORY_IN; Min[31:0] = MEMORY_OUT; W_ASCCI = Write_ASCII

  // Notes on the sheet:
  //   Input
  //   ASM
  //   Output
endmodule

module Task_66_Data_Path (
  input  [31:0] Value,
  input  Lcount,
  input  Scount,
  input  Ldir,
  input  Ln,
  input  Le2,
  input  Le1,
  input  Ln2,
  input  Ln1,
  input  Lcount2,
  input  Lcount1,
  input  Scount2,
  input  Scount1,
  input  Ldir2,
  input  Ldir1,
  input  Sdir2,
  input  CLK,
  input  Reset,
  output [23:0] Dir_1,
  output [23:0] Dir1o2,
  output [31:0] E1o2,
  output e1_e2,
  output count1_n1,
  output count2_n2,
  output count___n1_n2
);

  wire [23:0] bit_extender_1_out, bit_extender_2_out, Dir1, Dir1_1, Dir2, Dir2_1, Dir_1_t, multiplexer_1_out,
       multiplexer_5_out, Odir2, Odir2_1;
  wire [31:0] count, count1, count1_1, count2, count2_1, count_1, e1, e2, multiplexer_2_out,
       multiplexer_3_out, multiplexer_4_out, multiplexer_6_out, n, n1, n1_n2, n2;

  Adder #(.width(32)) adder_1 (.a(n1), .b(n2), .out(n1_n2));  // open: cin, cout
  Register #(.width(32)) Rn1 (.D(Value), .en(Ln1), .Q(n1), .clk(CLK), .clr(Reset));
  Register #(.width(32)) Re1 (.D(Value), .en(Le1), .Q(e1), .clk(CLK), .clr(Reset));
  Register #(.width(32)) Rn2 (.D(Value), .en(Ln2), .Q(n2), .clk(CLK), .clr(Reset));
  Register #(.width(32)) Re2 (.D(Value), .en(Le2), .Q(e2), .clk(CLK), .clr(Reset));
  Register #(.width(32)) Rn (.D(n1_n2), .en(Ln), .Q(n), .clk(CLK), .clr(Reset));
  Bit_Extender #(.in_width(32), .out_width(24)) bit_extender_1 (.in(n1), .out(bit_extender_1_out));
  Register #(.width(24)) RDir1 (.D(Dir1_1), .en(Ldir1), .Q(Dir1), .clk(CLK), .clr(Reset));
  Adder #(.width(24)) adder_2 (.a(Dir1), .b(24'h1), .out(Dir1_1));  // open: cin, cout
  Multiplexer #(.width(24), .disabled(0), .enable("false")) multiplexer_1 (
    .in0(Dir2_1), .in1(Odir2_1), .out(multiplexer_1_out), .sel(Sdir2));
  Adder #(.width(24)) adder_3 (.a(Dir2), .b(24'h1), .out(Dir2_1));  // open: cin, cout
  Adder #(.width(24)) adder_4 (.a(bit_extender_1_out), .b(24'h1), .out(Odir2));  // open: cin, cout
  Register #(.width(24)) RDir (.D(Dir_1_t), .en(Ldir), .Q(Dir_1), .clk(CLK), .clr(Reset));
  Adder #(.width(24)) adder_5 (.a(Dir_1), .b(24'h1), .out(Dir_1_t));  // open: cin, cout
  Register #(.width(24)) RDir2 (.D(multiplexer_1_out), .en(Ldir2), .Q(Dir2), .clk(CLK), .clr(Reset));
  Multiplexer #(.width(32), .disabled(0), .enable("false")) multiplexer_2 (
    .in0(32'h1), .in1(count1_1), .out(multiplexer_2_out), .sel(Scount1));
  Adder #(.width(32)) adder_6 (.a(count1), .b(32'h1), .out(count1_1));  // open: cin, cout
  Multiplexer #(.width(32), .disabled(0), .enable("false")) multiplexer_3 (
    .in0(32'h1), .in1(count2_1), .out(multiplexer_3_out), .sel(Scount2));
  Bit_Extender #(.in_width(32), .out_width(24)) bit_extender_2 (.in(n1), .out(bit_extender_2_out));
  Multiplexer #(.width(32), .disabled(0), .enable("false")) multiplexer_4 (
    .in0(32'h1), .in1(count_1), .out(multiplexer_4_out), .sel(Scount));
  Adder #(.width(32)) adder_7 (.a(count), .b(32'h1), .out(count_1));  // open: cin, cout
  Register #(.width(32)) Rcount1 (.D(multiplexer_2_out), .en(Lcount1), .Q(count1), .clk(CLK), .clr(Reset));
  Register #(.width(32)) Rcount2 (.D(multiplexer_3_out), .en(Lcount2), .Q(count2), .clk(CLK), .clr(Reset));
  Adder #(.width(32)) adder_8 (.a(count2), .b(32'h1), .out(count2_1));  // open: cin, cout
  Adder #(.width(24)) adder_9 (.a(bit_extender_2_out), .b(24'h2), .out(Odir2_1));  // open: cin, cout
  Register #(.width(32)) Rcount (.D(multiplexer_4_out), .en(Lcount), .Q(count), .clk(CLK), .clr(Reset));
  Multiplexer #(.width(24), .disabled(0), .enable("false")) multiplexer_5 (
    .in0(Dir1), .in1(Dir2), .out(multiplexer_5_out), .sel(Ldir2));
  Multiplexer #(.width(32), .disabled(0), .enable("false")) multiplexer_6 (
    .in0(e1), .in1(e2), .out(multiplexer_6_out), .sel(Ldir2));
  Multiplexer #(.width(24), .disabled(0), .enable("false")) multiplexer_7 (
    .in0(multiplexer_5_out), .in1(Odir2), .out(Dir1o2), .sel(Sdir2));
  Multiplexer #(.width(32), .disabled(0), .enable("false")) multiplexer_8 (
    .in0(multiplexer_6_out), .in1(n1_n2), .out(E1o2), .sel(Ln));
  Comparator #(.width(32), .mode("unsigned")) comparator_1 (.a(e1), .b(e2), .lt(e1_e2));  // open: gt, eq
  Comparator #(.width(32), .mode("unsigned")) comparator_2 (.a(count1), .b(n1), .lt(count1_n1));  // open: gt, eq
  Comparator #(.width(32), .mode("unsigned")) comparator_3 (.a(count2), .b(n2), .lt(count2_n2));  // open: gt, eq
  Comparator #(.width(32), .mode("unsigned")) comparator_4 (.a(count), .b(n), .lt(count___n1_n2));  // open: gt, eq

  // Other names for the same wires on the sheet: Dir[23:0] = Dir_1; Lc = Lcount; Lc1 = Lcount1; Lc2 = Lcount2;
  //   Sc = Scount; Sc1 = Scount1; Sc2 = Scount2

  // Notes on the sheet:
  //   Input
  //   Registers
  //   Output
  //   Flags
endmodule

module Task_66_Control_Unit (
  input  start,
  input  CLK,
  input  Reset,
  input  End_Print,
  input  e1_e2,
  input  count1_n1,
  input  count2_n2,
  input  count___n1_n2,
  output out_9,
  output out_10,
  output out_11,
  output out_12,
  output out_13,
  output out_14,
  output out_15,
  output out_16,
  output out_17,
  output out_18,
  output out_19,
  output out_20,
  output out_21,
  output out_22,
  output out_23,
  output Start_Print,
  output End
);

  wire demultiplexer_1_out0, demultiplexer_2_out1, demultiplexer_3_out0, demultiplexer_3_out1,
       demultiplexer_4_out0, demultiplexer_4_out1, demultiplexer_5_out0, demultiplexer_5_out1,
       demultiplexer_6_out0, demultiplexer_6_out1, IDLE_q, Ldir1_0, Ldir3, or_8_out, or_11_out, PRINT_q,
       WAIT_4_q, WHILE_q;

  D_Flip_Flop IDLE (.clk(CLK), .D(demultiplexer_1_out0), .Q(IDLE_q), .preset(Reset));  // open: Qn, en, reset
  Demultiplexer #(.disabled(0), .enable("false")) demultiplexer_1 (
    .out0(demultiplexer_1_out0), .out1(out_10), .in(IDLE_q), .sel(start));
  D_Flip_Flop WAIT (.clk(CLK), .D(out_10), .Q(out_15), .reset(Reset));  // open: Qn, preset, en
  D_Flip_Flop WAIT_2 (.clk(CLK), .D(out_15), .Q(Ldir1_0), .reset(Reset));  // open: Qn, preset, en
  D_Flip_Flop WAIT_3 (.clk(CLK), .D(Ldir1_0), .Q(out_20), .reset(Reset));  // open: Qn, preset, en
  D_Flip_Flop WAIT_4 (.clk(CLK), .D(out_20), .Q(WAIT_4_q), .reset(Reset));  // open: Qn, preset, en
  or or_1 (out_21, out_11, out_16);
  or or_2 (Ldir3, WAIT_4_q, out_21);
  or or_3 (out_16, demultiplexer_4_out0, demultiplexer_3_out0);
  or or_4 (out_11, demultiplexer_5_out0, demultiplexer_3_out1);
  or or_5 (out_23, out_20, out_21);
  D_Flip_Flop WHILE (.clk(CLK), .D(Ldir3), .Q(WHILE_q), .reset(Reset));  // open: Qn, preset, en
  Demultiplexer #(.disabled(0), .enable("false")) demultiplexer_2 (
    .out0(Start_Print), .out1(demultiplexer_2_out1), .in(WHILE_q), .sel(count___n1_n2));
  Demultiplexer #(.disabled(0), .enable("false")) demultiplexer_3 (
    .out0(demultiplexer_3_out0), .out1(demultiplexer_3_out1), .in(demultiplexer_5_out1), .sel(e1_e2));
  or or_6 (out_9, Ldir1_0, out_11);
  or or_7 (out_13, out_11, Ldir1_0, out_10);
  Demultiplexer #(.disabled(0), .enable("false")) demultiplexer_4 (
    .out0(demultiplexer_4_out0), .out1(demultiplexer_4_out1), .in(demultiplexer_2_out1), .sel(count1_n1));
  Demultiplexer #(.disabled(0), .enable("false")) demultiplexer_5 (
    .out0(demultiplexer_5_out0), .out1(demultiplexer_5_out1), .in(demultiplexer_4_out1), .sel(count2_n2));
  or or_8 (or_8_out, demultiplexer_6_out0, Start_Print);
  D_Flip_Flop PRINT (.clk(CLK), .D(or_8_out), .Q(PRINT_q), .reset(Reset));  // open: Qn, preset, en
  Demultiplexer #(.disabled(0), .enable("false")) demultiplexer_6 (
    .out0(demultiplexer_6_out0), .out1(demultiplexer_6_out1), .in(PRINT_q), .sel(End_Print));
  or or_9 (out_14, out_20, out_16);
  or or_10 (out_18, out_15, out_20, out_16);
  or or_11 (or_11_out, demultiplexer_6_out1, End);
  D_Flip_Flop u_END (.clk(CLK), .D(or_11_out), .Q(End), .reset(Reset));  // open: Qn, preset, en

  assign out_12 = out_11;
  assign out_17 = out_16;
  assign out_19 = out_15;
  assign out_22 = out_21;

  // Other names for the same wires on the sheet: Ldir = out_23; Ldir1 = out_13; Ldir2 = out_18; Le1 = out_9;
  //   Le1_0 = Ldir1_0; Le2 = out_14; Ldir2_1 = out_20; Ldir_0 = out_20; Le2_0 = out_20; Ln = out_20; Ldir1_3 = out_10;
  //   Ln1 = out_10; Lc = out_21; Ldir_1 = out_21; Sc = out_21; Lc1 = out_11; Ldir1_1 = out_11; Le1_1 = out_11;
  //   Sc1 = out_11; Lc2 = out_16; Ldir2_2 = out_16; Le2_1 = out_16; Sc2 = out_16; Ldir2_0 = out_15; Ln2 = out_15;
  //   Sdir2 = out_15

  // Notes on the sheet:
  //   Output
  //   Input
endmodule
